# Fritzing sketch rpaper_layout (saved by Fritzing 0.9.3b)
circuit board: 8.46667cm x 5.64444cm

parts:
  U1 = NodeMCU V3.0
  OLED1 = 128x64 Monochrom OLED Display with SPI Control
  BAT1 = 18650 battery holder [package=battery-18650-kit]
  S1 = Pushbutton [package=THT]
  S2 = Toggle Switch [package=THT]  # not connected

nets (from the schematic view):
  N1: U1.D0, U1.RST
  N2: U1.D1, OLED1.Reset
  N3: U1.D2, S1.leg1
  N4: U1.D3, OLED1.SA0/DC
  N5: U1.D4, OLED1.Clock
  3V3: U1.3V3, OLED1.Vin
  N6: U1.GND#6, U1.GND#13, OLED1.GND, BAT1.-
  N7: U1.D5, OLED1.3v3
  N8: U1.D6, OLED1.Data
  N9: U1.D7, OLED1.CS
  N10: U1.Vin, BAT1.+
  N11: U1.GND#41, S1.leg0

notes:
  BUSY => D6
  RST => D4
  DC => D3
  CS => D1
  DIN => D7
  CLK => D5
  VCC => 3V3
  GND => GND

custom parts:
  NodeMCU V3.0: ESP8266 based NodeMCU
  18650 battery holder: 18650 Battery Holder
